// Digital circuit CompA2.dig as structural Verilog
module CompA2 (
  input  Sign,
  input  A0,
  input  A1,
  input  A2,
  input  A3,
  output B0,
  output B1,
  output B2,
  output B3
);

  wire semis_1_cout, semis_2_cout, semis_3_cout, xor_1_out, xor_2_out, xor_3_out, xor_4_out;

  xor xor_1 (xor_1_out, A0, Sign);
  xor xor_2 (xor_2_out, A1, Sign);
  xor xor_3 (xor_3_out, A2, Sign);
  xor xor_4 (xor_4_out, A3, Sign);
  SemiS semis_1 (.a(Sign), .b(xor_1_out), .Sum(B0), .Cout(semis_1_cout));
  SemiS semis_2 (.a(semis_1_cout), .b(xor_2_out), .Sum(B1), .Cout(semis_2_cout));
  SemiS semis_3 (.a(semis_2_cout), .b(xor_3_out), .Sum(B2), .Cout(semis_3_cout));
  xor xor_5 (B3, semis_3_cout, xor_4_out);
endmodule
