// Digital circuit SumRes.dig as structural Verilog
module SumRes (
  input  A0,
  input  A1,
  input  A2,
  input  A3,
  input  SA,
  input  B0,
  input  B1,
  input  B2,
  input  B3,
  input  SB,
  output C0,
  output C1,
  output C2,
  output C3,
  output SC
);

  wire and_1_out, compa2_1_b0, compa2_1_b1, compa2_1_b2, compa2_1_b3, compa2_2_b0, compa2_2_b1, compa2_2_b2,
       compa2_2_b3, sumador4b_1_cout, sumador4b_1_s0, sumador4b_1_s1, sumador4b_1_s2, sumador4b_1_s3,
       sumador_1_sum;

  and and_1 (and_1_out, SA, SB);
  CompA2 compa2_1 (
    .Sign(SA), .A0(A0), .A1(A1), .A2(A2), .A3(A3), .B0(compa2_1_b0), .B1(compa2_1_b1), .B2(compa2_1_b2),
    .B3(compa2_1_b3));
  CompA2 compa2_2 (
    .Sign(SB), .A0(B0), .A1(B1), .A2(B2), .A3(B3), .B0(compa2_2_b0), .B1(compa2_2_b1), .B2(compa2_2_b2),
    .B3(compa2_2_b3));
  Sumador4b sumador4b_1 (
    .a0(compa2_1_b0), .a1(compa2_1_b1), .b0(compa2_2_b0), .b1(compa2_2_b1), .cin(1'b0), .a2(compa2_1_b2),
    .b2(compa2_2_b2), .a3(compa2_1_b3), .b3(compa2_2_b3), .s0(sumador4b_1_s0), .s1(sumador4b_1_s1),
    .s2(sumador4b_1_s2), .s3(sumador4b_1_s3), .cout(sumador4b_1_cout));
  Sumador sumador_1 (.a(SA), .b(SB), .c(sumador4b_1_cout), .Sum(sumador_1_sum));  // open: Cout
  Multiplexer multiplexer_1 (.sel(and_1_out), .in_0(sumador_1_sum), .in_1(and_1_out), .out(SC));
  CompA2 compa2_3 (
    .Sign(SC), .A0(sumador4b_1_s0), .A1(sumador4b_1_s1), .A2(sumador4b_1_s2), .A3(sumador4b_1_s3), .B0(C0),
    .B1(C1), .B2(C2), .B3(C3));
endmodule
