// Digital circuit Sumador.dig as structural Verilog
module Sumador (
  input  a,
  input  b,
  input  c,
  output Sum,
  output Cout
);

  wire semis_1_cout, semis_1_sum, semis_2_cout;

  SemiS semis_1 (.a(a), .b(b), .Sum(semis_1_sum), .Cout(semis_1_cout));
  SemiS semis_2 (.a(semis_1_sum), .b(c), .Sum(Sum), .Cout(semis_2_cout));
  or or_1 (Cout, semis_2_cout, semis_1_cout);
endmodule
