// Digital circuit Sumador4b.dig as structural Verilog
module Sumador4b (
  input  a0,
  input  a1,
  input  b0,
  input  b1,
  input  cin,
  input  a2,
  input  b2,
  input  a3,
  input  b3,
  output s0,
  output s1,
  output s2,
  output s3,
  output cout
);

  wire sumador_1_cout, sumador_2_cout, sumador_3_cout;

  Sumador sumador_1 (.a(a0), .b(b0), .c(cin), .Sum(s0), .Cout(sumador_1_cout));
  Sumador sumador_2 (.a(a1), .b(b1), .c(sumador_1_cout), .Sum(s1), .Cout(sumador_2_cout));
  Sumador sumador_3 (.a(a2), .b(b2), .c(sumador_2_cout), .Sum(s2), .Cout(sumador_3_cout));
  Sumador sumador_4 (.a(a3), .b(b3), .c(sumador_3_cout), .Sum(s3), .Cout(cout));
endmodule
